# Fritzing sketch BoardLayput (saved by Fritzing 0.9.3b)
breadboards: 1

parts:
  LED1 = LEDs [package=led10mm]
  Part2 = Soil Moisture Sensor
  Part3 = Soil Moisture Sensor
  R1 = Resistor [tolerance=±5% resistance=470 package="0603 [SMD]"]
  Part4 = Arduino MicroSD Shield  # not connected
  Part1 = Arduino Uno (Rev3)

nets:
  N1: LED1.C, R1.Pin_0
  GND: LED1.A, Part2.GND, Part3.GND, Part1.GND
  N2: Part2.SIG, Part1.A1
  VCC: Part2.VCC, Part3.VCC, Part1.D7
  N3: Part3.SIG, Part1.A0
  N4: R1.Pin_1, Part1.D8
