# Fritzing sketch Temperatutor (saved by Fritzing 0.5.2b)
breadboards: 1

parts:
  Arduino1 = Arduino
  IC1 = IC, DIP package, 8 pins [chip_label=TMP102 spacing=300mil]
  LED1 = Red LED - 5mm [package="5 mm [THT]"]
  LED2 = Blue LED - 5mm [package="5 mm [THT]"]
  R2 = Rotary Potentiometer (Small)
  R1 = Rotary Potentiometer (Small)

nets:
  N1: Arduino1.D11, LED1.anode
  N2: Arduino1.D10, LED2.anode
  N3: Arduino1.3V3, IC1.pin1
  N4: Arduino1.+5V, R2.leg2, R1.leg1
  N5: Arduino1.GND, IC1.pin4, IC1.pin7, LED1.cathode, LED2.cathode, R2.leg1, R1.leg2
  N6: Arduino1.A0, R1.wiper
  N7: Arduino1.A1, R2.wiper
  N8: Arduino1.A4, IC1.pin2
  N9: Arduino1.A5, IC1.pin3
